# Fritzing sketch схема (saved by Fritzing 0.9.3b)
breadboards: 2

parts:
  Display1 = 4-Digit 7-segment LED Display [package=THT]
  Часть2 = Arduino Nano (Rev3.0)
  S1 = Pushbutton [package="[THT]"]  # not connected

nets:
  N1: Display1.GND, Часть2.D3
  N2: Display1.VCC, Часть2.D4

custom parts:
  4-Digit 7-segment LED Display: A 4-digit 7-segments LED display PCB module driven by a TM1637 control IC via 1-wire protocol.
